// Logisim project COD 3 78.circ as structural Verilog: 1 circuit, main circuit main
module main (
  input  A,
  input  B,
  input  A_2,
  input  B_2,
  input  CIN,
  output SUM,
  output CARRY,
  output SUM_2,
  output CARRY_2
);

  wire and_2_out, and_3_out, xor_2_out;

  xor xor_1 (SUM, A, B);
  and and_1 (CARRY, A, B);
  xor xor_2 (xor_2_out, A_2, B_2);
  and and_2 (and_2_out, A_2, B_2);
  xor xor_3 (SUM_2, xor_2_out, CIN);
  and and_3 (and_3_out, xor_2_out, CIN);
  or or_1 (CARRY_2, and_3_out, and_2_out);

  // Notes on the sheet:
  //   HALF ADDER
  //   FULL ADDER
  //   A
  //   B
  //                                                                      HALF ADDER & FULL ADDER
endmodule
